# Fritzing sketch FritzEspRelay (saved by Fritzing 0.9.3b)

parts:
  WeMos_D1_Mini1 = WeMos D1 Mini
  U4 = RELAY [package=relay-t9a]
  U5 = Transformer [package=transformer]
  Q1 = NPN-Transistor [package="TO92 [THT]"]

nets:
  N1: WeMos_D1_Mini1.5V, U4.COIL2, U5.3, Q1.E
  N2: WeMos_D1_Mini1.D3, Q1.B
  N3: WeMos_D1_Mini1.G, U4.COIL1, U5.4
  N4: U4.MAIN, Q1.C

notes:
  220V input
  Load - heater (2kW)
